// Logisim project 08-08-2024.circ as structural Verilog: 5 circuits, main circuit main
module main (
  input  in_1
);

  wire somador4bits_1_out_9, somador4bits_1_out_10, somador4bits_1_out_11, somador4bits_1_out_12, undriven;

  somador4Bits somador4bits_1 (
    .x1(in_1), .x2(undriven), .out_9(somador4bits_1_out_9), .out_10(somador4bits_1_out_10),
    .out_11(somador4bits_1_out_11), .out_12(somador4bits_1_out_12));  // open: x3, x4, y1, y2, y3, y4
  decodificador decodificador_1 (
    .a(somador4bits_1_out_9), .b(somador4bits_1_out_10), .c(somador4bits_1_out_11), .d(somador4bits_1_out_12));  // open: x, y, z, u, v, w, s
endmodule

module somaCompleta (
  input  vem1,
  input  x,
  input  y,
  output S,
  output vai1
);

  wire meiasoma_1_s, meiasoma_1_vai1, meiasoma_2_vai1;

  meiaSoma meiasoma_1 (.X(x), .Y(y), .S(meiasoma_1_s), .Vai1(meiasoma_1_vai1));
  or or_1 (vai1, meiasoma_1_vai1, meiasoma_2_vai1);
  meiaSoma meiasoma_2 (.X(vem1), .Y(meiasoma_1_s), .S(S), .Vai1(meiasoma_2_vai1));
endmodule

module meiaSoma (
  input  X,
  input  Y,
  output S,
  output Vai1
);

  xor xor_1 (S, X, Y);
  and and_1 (Vai1, Y, X);
endmodule

module somador4Bits (
  input  x1,
  input  x2,
  input  x3,
  input  x4,
  input  y1,
  input  y2,
  input  y3,
  input  y4,
  output out_9,
  output out_10,
  output out_11,
  output out_12
);

  wire somacompleta_1_vai1, somacompleta_2_vai1, somacompleta_3_vai1;

  somaCompleta somacompleta_1 (.x(x1), .y(y1), .vem1(1'b0), .vai1(somacompleta_1_vai1), .S(out_9));
  somaCompleta somacompleta_2 (.x(x2), .y(y2), .vem1(somacompleta_1_vai1), .vai1(somacompleta_2_vai1), .S(out_10));
  somaCompleta somacompleta_3 (.x(x3), .y(y3), .vem1(somacompleta_2_vai1), .vai1(somacompleta_3_vai1), .S(out_11));
  somaCompleta somacompleta_4 (.x(x4), .y(y4), .vem1(somacompleta_3_vai1), .S(out_12));  // open: vai1
endmodule

module decodificador (
  input  a,
  input  b,
  input  c,
  input  d,
  output x,
  output y,
  output z,
  output u,
  output v,
  output w,
  output s
);

  wire and_1_out, and_2_out, and_3_out, and_4_out, and_5_out, and_6_out, and_7_out, and_8_out, and_9_out,
       and_10_out, and_11_out, and_12_out, and_13_out, and_14_out, and_15_out, and_16_out, and_17_out,
       and_18_out, and_19_out, and_20_out, and_21_out, and_22_out, and_23_out, and_24_out, and_25_out,
       and_26_out, and_27_out, and_28_out, and_29_out, and_30_out, and_31_out, and_32_out, and_33_out,
       and_34_out, and_35_out, and_36_out, not_1_out, not_2_out, not_3_out, not_4_out, not_5_out, not_6_out,
       not_7_out, not_8_out, not_9_out, not_10_out, not_11_out, not_12_out, not_13_out, not_14_out,
       not_15_out, not_16_out, not_17_out, not_18_out, not_19_out, not_20_out, not_21_out, not_22_out,
       not_23_out, not_24_out, not_25_out, not_26_out, not_27_out, not_28_out, not_29_out, not_30_out,
       not_31_out, not_32_out, not_33_out, not_34_out, not_35_out, not_36_out, not_37_out, not_38_out,
       not_39_out, not_40_out, not_41_out, not_42_out, not_43_out, not_44_out, not_45_out, not_46_out,
       not_47_out;

  not not_1 (not_1_out, b);
  and and_1 (and_1_out, not_1_out, not_2_out);
  not not_2 (not_2_out, d);
  not not_3 (not_3_out, a);
  not not_4 (not_4_out, b);
  and and_2 (and_2_out, not_3_out, not_4_out, c);
  not not_5 (not_5_out, a);
  and and_3 (and_3_out, not_5_out, b, d);
  not not_6 (not_6_out, b);
  and and_4 (and_4_out, a, not_6_out, not_7_out);
  not not_7 (not_7_out, c);
  and and_5 (and_5_out, a, not_8_out);
  not not_8 (not_8_out, d);
  and and_6 (and_6_out, a, b, c);
  not not_9 (not_9_out, a);
  and and_7 (and_7_out, not_9_out, not_10_out);
  not not_10 (not_10_out, b);
  not not_11 (not_11_out, a);
  and and_8 (and_8_out, not_11_out, not_12_out, not_13_out);
  not not_12 (not_12_out, c);
  not not_13 (not_13_out, d);
  not not_14 (not_14_out, b);
  and and_9 (and_9_out, not_14_out, not_15_out);
  not not_15 (not_15_out, c);
  not not_16 (not_16_out, b);
  and and_10 (and_10_out, not_16_out, not_17_out);
  not not_17 (not_17_out, d);
  not not_18 (not_18_out, a);
  and and_11 (and_11_out, not_18_out, c, d);
  not not_19 (not_19_out, c);
  and and_12 (and_12_out, a, not_19_out, d);
  not not_20 (not_20_out, a);
  and and_13 (and_13_out, not_20_out, not_21_out);
  not not_21 (not_21_out, c);
  not not_22 (not_22_out, a);
  and and_14 (and_14_out, not_22_out, d);
  not not_23 (not_23_out, c);
  and and_15 (and_15_out, not_23_out, d);
  not not_24 (not_24_out, a);
  and and_16 (and_16_out, not_24_out, b);
  and and_17 (and_17_out, a, not_25_out);
  not not_25 (not_25_out, b);
  not not_26 (not_26_out, a);
  and and_18 (and_18_out, not_26_out, not_27_out, not_28_out);
  not not_27 (not_27_out, b);
  not not_28 (not_28_out, d);
  not not_29 (not_29_out, b);
  and and_19 (and_19_out, not_29_out, c, d);
  and and_20 (and_20_out, b, not_30_out, d);
  not not_30 (not_30_out, c);
  and and_21 (and_21_out, b, c, not_31_out);
  not not_31 (not_31_out, d);
  not not_32 (not_32_out, c);
  and and_22 (and_22_out, a, not_32_out, not_33_out);
  not not_33 (not_33_out, d);
  not not_34 (not_34_out, b);
  and and_23 (and_23_out, not_34_out, not_35_out);
  not not_35 (not_35_out, d);
  and and_24 (and_24_out, c, not_36_out);
  not not_36 (not_36_out, d);
  and and_25 (and_25_out, a, c);
  and and_26 (and_26_out, a, b);
  not not_37 (not_37_out, c);
  and and_27 (and_27_out, not_37_out, not_38_out);
  not not_38 (not_38_out, d);
  not not_39 (not_39_out, a);
  and and_28 (and_28_out, not_39_out, b, not_40_out);
  not not_40 (not_40_out, c);
  and and_29 (and_29_out, b, not_41_out);
  not not_41 (not_41_out, d);
  and and_30 (and_30_out, a, not_42_out);
  not not_42 (not_42_out, b);
  and and_31 (and_31_out, a, c);
  not not_43 (not_43_out, b);
  and and_32 (and_32_out, not_43_out, c);
  and and_33 (and_33_out, c, not_44_out);
  not not_44 (not_44_out, d);
  not not_45 (not_45_out, a);
  and and_34 (and_34_out, not_45_out, b, not_46_out);
  not not_46 (not_46_out, c);
  and and_35 (and_35_out, a, not_47_out);
  not not_47 (not_47_out, b);
  and and_36 (and_36_out, a, d);
  or or_1 (z, and_13_out, and_14_out, and_15_out, and_16_out, and_17_out);
  or or_2 (u, and_18_out, and_19_out, and_20_out, and_21_out, and_22_out);
  or or_3 (v, and_23_out, and_24_out, and_25_out, and_26_out);
  or or_4 (w, and_27_out, and_28_out, and_29_out, and_30_out, and_31_out);
  or or_5 (s, and_32_out, and_33_out, and_34_out, and_35_out, and_36_out);
  or or_6 (x, and_1_out, and_2_out, and_3_out, and_4_out, and_5_out, and_6_out);
  or or_7 (y, and_7_out, and_8_out, and_9_out, and_10_out, and_11_out, and_12_out);
endmodule
